// Logisim project project-v1.circ as structural Verilog: 9 circuits, main circuit main
module main (
  input  in_1,
  input  in_2,
  input  in_3,
  input  in_4,
  input  in_5,
  input  in_6,
  input  in_7,
  input  in_8,
  input  in_9,
  input  ir3,
  input  ir2,
  input  ir1,
  input  ir0
);

  wire add_1_out0, add_1_out1, add_1_out2, add_1_out3, add_sub, adr, adr0en, adr1en, and_1_out, and_2_out,
       and_3_out, and_4_out, and_5_out, and_6_out, and_7_out, and_8_out, clock, d0, d1, d2, d3, L0, L1, L2,
       L3, L_in0, L_in1, L_in2, L_in3, not_1_out, or_1_out, or_2_out, or_3_out, or_4_out, R0, R1, r1_b0,
       r1_b1, r1_b2, r1_b3, R2, R3, reg0en, reg0write, reg1en, reg1write;

  _7_Segment_Display u_7_segment_display_1 ();  // open: g, f, a, b, e, d, c, dp
  _7_Segment_Display u_7_segment_display_2 ();  // open: g, f, a, b, e, d, c, dp
  Clock clock_1 (.out(clock));
  RAMx ramx_1 ();  // open: adr2, adr1, adr0, mode, clock, in3, in2, in1, in0, out3, out2, out1, out0
  or or_1 (or_1_out, d3, add_1_out3, r1_b3, L3);
  or or_2 (or_2_out, d2, add_1_out2, r1_b2, L2);
  or or_3 (or_3_out, d1, add_1_out1, r1_b1, L1);
  or or_4 (or_4_out, d0, add_1_out0, L0);
  reg4bits u_r0 (
    .d3(or_1_out), .d2(or_2_out), .d1(or_3_out), .d0(or_4_out), .en(reg0en), .clk(clock), .rw(reg0write),
    .b3(L3), .b2(L2), .b1(L1), .b0(L0));
  reg4bits u_r1 (
    .d3(or_1_out), .d2(or_2_out), .d1(or_3_out), .d0(or_4_out), .en(reg1en), .clk(clock), .rw(reg1write),
    .b3(r1_b3), .b2(r1_b2), .b1(r1_b1), .b0(r1_b0));
  not not_1 (not_1_out, ir3);
  or or_5 (R3, L3, r1_b3);
  or or_6 (R2, L2, r1_b2);
  or or_7 (R1, L1, r1_b1);
  or or_8 (R0, L0, r1_b0);
  PC pc_1 (.adr1(not_1_out), .adr0(ir3));  // open: in_en, adr3, adr2, en, clock, rw, out3, out2, out1, out0
  MBR mbr_1 (.adr(ir3));  // open: b3, b2, b1, b0
  CU cu_1 (
    .clock(clock), .ir3(ir3), .ir2(ir2), .ir1(ir1), .ir0(ir0), .reg0write(reg0write), .reg0en(reg0en),
    .reg1write(reg1write), .reg1en(reg1en), .adr0write(adr), .adr0en(adr0en), .adr1write(adr),
    .adr1en(adr1en), .add_sub(add_sub));  // open: s3, s2, s1, s0
  ADD add_1 (
    .out0(add_1_out0), .out3(add_1_out3), .out2(add_1_out2), .out1(add_1_out1), .R3(R3), .R2(R2), .R1(R1),
    .R0(R0), .command(add_sub), .clock(clock), .L3(L3), .L2(L2), .L1(L1), .L0(L0));  // open: status0, status1, status2
  and and_1 (and_1_out, L3, reg0en);
  and and_2 (and_2_out, R3, reg1en);
  and and_3 (and_3_out, L2, reg0en);
  and and_4 (and_4_out, R2, reg1en);
  and and_5 (and_5_out, L1, reg0en);
  and and_6 (and_6_out, R1, reg1en);
  and and_7 (and_7_out, L0, reg0en);
  and and_8 (and_8_out, R0, reg1en);
  or or_9 (L_in3, and_1_out, and_2_out);
  or or_10 (L_in2, and_3_out, and_4_out);
  or or_11 (L_in1, and_5_out, and_6_out);
  or or_12 (L_in0, and_7_out, and_8_out);
  RAMx ramx_2 (
    .adr2(clock), .mode(adr), .clock(1'b0), .out3(d3), .out2(d2), .out1(d1), .out0(d0));  // open: adr1, adr0, in3, in2, in1, in0
  RAMx ramx_3 (
    .adr2(clock), .mode(adr), .clock(1'b1), .in3(L_in3), .in2(L_in2), .in1(L_in1), .in0(L_in0));  // open: adr1, adr0, out3, out2, out1, out0

  // Other names for the same wires on the sheet: address = in_1; adr0write = adr; adr1write = adr; in0_1 = in_9;
  //   in0_2 = in_5; in1_1 = in_8; in1_2 = in_4; in2_1 = in_7; in2_2 = in_3; in3_1 = in_6; in3_2 = in_2

  // Notes on the sheet:
  //   Winifred Jia (260988523)
  //   Venicia Leblanc (261054489)
  //   address
  //   input 2
  //   bus
  //   input 1
  //   save address 0/1 in R0/R1
  //   load R0/R1 in address 0/1
endmodule

module reg4bits (
  input  d3,
  input  d2,
  input  d1,
  input  d0,
  input  en,
  input  clk,
  input  rw,
  output b3,
  output b2,
  output b1,
  output b0
);

  wire and_1_out, d_ff_1_q, d_ff_2_q, d_ff_3_q, d_ff_4_q;

  and and_1 (and_1_out, clk, rw);
  D_Flip_Flop d_ff_1 (.D(d0), .clk(and_1_out), .Q(d_ff_1_q));  // open: Qn, preset, reset
  D_Flip_Flop d_ff_2 (.D(d1), .clk(and_1_out), .Q(d_ff_2_q));  // open: Qn, preset, reset
  D_Flip_Flop d_ff_3 (.D(d2), .clk(and_1_out), .Q(d_ff_3_q));  // open: Qn, preset, reset
  D_Flip_Flop d_ff_4 (.D(d3), .clk(and_1_out), .Q(d_ff_4_q));  // open: Qn, preset, reset
  and and_2 (b0, en, d_ff_1_q);
  and and_3 (b1, en, d_ff_2_q);
  and and_4 (b2, en, d_ff_3_q);
  and and_5 (b3, en, d_ff_4_q);

  // Notes on the sheet:
  //   Input
  //   1 = write
  //   0 = read
  //   Output
endmodule

module RAMx (
  input  adr2,
  input  adr1,
  input  adr0,
  input  mode,
  input  clock,
  input  in3,
  input  in2,
  input  in1,
  input  in0,
  output out3,
  output out2,
  output out1,
  output out0
);

  wire and_1_out, and_2_out, and_3_out, and_4_out, and_5_out, and_6_out, and_7_out, and_8_out, and_9_out,
       and_10_out, and_11_out, and_12_out, and_13_out, and_14_out, and_15_out, and_16_out, and_17_out,
       and_18_out, and_19_out, and_20_out, and_21_out, and_22_out, and_23_out, and_24_out, and_25_out,
       and_26_out, and_27_out, and_28_out, and_29_out, and_30_out, and_31_out, and_32_out, and_33_out,
       and_34_out, and_35_out, and_36_out, and_37_out, and_38_out, and_39_out, and_40_out, and_41_out,
       and_42_out, and_43_out, and_44_out, and_45_out, and_46_out, and_47_out, and_48_out, and_49_out,
       and_50_out, and_51_out, and_52_out, and_53_out, and_54_out, and_55_out, and_56_out, and_57_out,
       and_58_out, and_59_out, and_60_out, and_61_out, and_62_out, and_63_out, and_64_out, and_65_out,
       and_66_out, and_67_out, and_68_out, and_69_out, and_70_out, and_71_out, and_72_out, and_73_out,
       and_74_out, and_75_out, and_76_out, and_77_out, and_78_out, and_79_out, and_80_out, d_ff_1_q,
       d_ff_2_q, d_ff_3_q, d_ff_4_q, d_ff_5_q, d_ff_6_q, d_ff_7_q, d_ff_8_q, d_ff_9_q, d_ff_10_q, d_ff_11_q,
       d_ff_12_q, d_ff_13_q, d_ff_14_q, d_ff_15_q, d_ff_17_q, d_ff_18_q, d_ff_19_q, d_ff_20_q, d_ff_21_q,
       d_ff_22_q, d_ff_23_q, d_ff_24_q, d_ff_25_q, d_ff_29_q, d_ff_30_q, d_ff_31_q, d_ff_32_q, d_ff_33_q,
       d_ff_34_q, d_ff_35_q, d_ff_36_q, d_ff_37_q, d_ff_38_q, d_ff_39_q, d_ff_40_q, d_ff_41_q, d_ff_42_q,
       d_ff_43_q, d_ff_44_q, not_1_out, not_2_out, not_3_out, not_4_out, not_5_out, not_6_out, not_7_out,
       not_8_out, not_9_out, not_10_out, not_11_out, not_12_out, not_13_out, or_1_out, or_2_out, or_3_out,
       or_4_out;

  D_Flip_Flop d_ff_1 (.D(adr2), .clk(clock), .Q(d_ff_1_q));  // open: Qn, preset, reset
  D_Flip_Flop d_ff_2 (.D(adr1), .clk(clock), .Q(d_ff_2_q));  // open: Qn, preset, reset
  not not_1 (not_1_out, d_ff_3_q);
  not not_2 (not_2_out, d_ff_2_q);
  not not_3 (not_3_out, d_ff_2_q);
  not not_4 (not_4_out, d_ff_3_q);
  not not_5 (not_5_out, d_ff_1_q);
  not not_6 (not_6_out, d_ff_1_q);
  not not_7 (not_7_out, d_ff_3_q);
  not not_8 (not_8_out, d_ff_1_q);
  not not_9 (not_9_out, d_ff_2_q);
  not not_10 (not_10_out, d_ff_1_q);
  not not_11 (not_11_out, d_ff_2_q);
  not not_12 (not_12_out, d_ff_3_q);
  D_Flip_Flop d_ff_3 (.D(adr0), .clk(clock), .Q(d_ff_3_q));  // open: Qn, preset, reset
  and and_1 (and_1_out, d_ff_1_q, d_ff_2_q, clock, d_ff_3_q);
  and and_2 (and_2_out, d_ff_1_q, d_ff_2_q, clock, not_1_out);
  and and_3 (and_3_out, d_ff_1_q, not_2_out, clock, d_ff_3_q);
  and and_4 (and_4_out, d_ff_1_q, not_3_out, clock, not_4_out);
  and and_5 (and_5_out, not_5_out, d_ff_2_q, clock, d_ff_3_q);
  and and_6 (and_6_out, not_6_out, d_ff_2_q, clock, not_7_out);
  and and_7 (and_7_out, not_8_out, not_9_out, clock, d_ff_3_q);
  and and_8 (and_8_out, not_10_out, not_11_out, clock, not_12_out);
  and and_9 (and_9_out, and_1_out, d_ff_4_q);
  and and_10 (and_10_out, and_2_out, d_ff_4_q);
  and and_11 (and_11_out, and_3_out, d_ff_4_q);
  and and_12 (and_12_out, and_4_out, d_ff_4_q);
  and and_13 (and_13_out, and_5_out, d_ff_4_q);
  and and_14 (and_14_out, and_6_out, d_ff_4_q);
  and and_15 (and_15_out, and_7_out, d_ff_4_q);
  and and_16 (and_16_out, and_8_out, d_ff_4_q);
  D_Flip_Flop d_ff_4 (.D(mode), .clk(clock), .Q(d_ff_4_q));  // open: Qn, preset, reset
  and and_17 (and_17_out, and_1_out, d_ff_4_q, d_ff_13_q);
  D_Flip_Flop #(.trigger("high")) d_ff_5 (.D(and_17_out), .clk(and_9_out), .Q(d_ff_5_q));  // open: Qn, preset, reset
  and and_18 (and_18_out, and_2_out, d_ff_4_q, d_ff_13_q);
  D_Flip_Flop #(.trigger("high")) d_ff_6 (.D(and_18_out), .clk(and_10_out), .Q(d_ff_6_q));  // open: Qn, preset, reset
  and and_19 (and_19_out, and_3_out, d_ff_4_q, d_ff_13_q);
  D_Flip_Flop #(.trigger("high")) d_ff_7 (.D(and_19_out), .clk(and_11_out), .Q(d_ff_7_q));  // open: Qn, preset, reset
  and and_20 (and_20_out, and_4_out, d_ff_4_q, d_ff_13_q);
  D_Flip_Flop #(.trigger("high")) d_ff_8 (.D(and_20_out), .clk(and_12_out), .Q(d_ff_8_q));  // open: Qn, preset, reset
  and and_21 (and_21_out, and_5_out, d_ff_4_q, d_ff_13_q);
  D_Flip_Flop #(.trigger("high")) d_ff_9 (.D(and_21_out), .clk(and_13_out), .Q(d_ff_9_q));  // open: Qn, preset, reset
  and and_22 (and_22_out, and_6_out, d_ff_4_q, d_ff_13_q);
  D_Flip_Flop #(.trigger("high")) d_ff_10 (.D(and_22_out), .clk(and_14_out), .Q(d_ff_10_q));  // open: Qn, preset, reset
  and and_23 (and_23_out, and_7_out, d_ff_4_q, d_ff_13_q);
  D_Flip_Flop #(.trigger("high")) d_ff_11 (.D(and_23_out), .clk(and_15_out), .Q(d_ff_11_q));  // open: Qn, preset, reset
  and and_24 (and_24_out, and_8_out, d_ff_4_q, d_ff_13_q);
  D_Flip_Flop #(.trigger("high")) d_ff_12 (.D(and_24_out), .clk(and_16_out), .Q(d_ff_12_q));  // open: Qn, preset, reset
  not not_13 (not_13_out, d_ff_4_q);
  and and_25 (and_25_out, d_ff_5_q, and_1_out, not_13_out);
  and and_26 (and_26_out, d_ff_6_q, and_2_out, not_13_out);
  and and_27 (and_27_out, d_ff_7_q, and_3_out, not_13_out);
  and and_28 (and_28_out, d_ff_8_q, and_4_out, not_13_out);
  and and_29 (and_29_out, d_ff_9_q, and_5_out, not_13_out);
  and and_30 (and_30_out, d_ff_10_q, and_6_out, not_13_out);
  and and_31 (and_31_out, d_ff_11_q, and_7_out, not_13_out);
  and and_32 (and_32_out, d_ff_12_q, and_8_out, not_13_out);
  D_Flip_Flop d_ff_13 (.D(in3), .clk(clock), .Q(d_ff_13_q));  // open: Qn, preset, reset
  or or_1 (or_1_out, and_25_out, and_26_out, and_27_out, and_28_out, and_29_out, and_30_out, and_31_out, and_32_out);
  D_Flip_Flop d_ff_14 (.D(in2), .clk(clock), .Q(d_ff_14_q));  // open: Qn, preset, reset
  and and_33 (and_33_out, and_1_out, d_ff_4_q, d_ff_14_q);
  and and_34 (and_34_out, and_2_out, d_ff_4_q, d_ff_14_q);
  and and_35 (and_35_out, and_3_out, d_ff_4_q, d_ff_14_q);
  and and_36 (and_36_out, and_4_out, d_ff_4_q, d_ff_14_q);
  and and_37 (and_37_out, and_5_out, d_ff_4_q, d_ff_14_q);
  and and_38 (and_38_out, and_6_out, d_ff_4_q, d_ff_14_q);
  and and_39 (and_39_out, and_7_out, d_ff_4_q, d_ff_14_q);
  and and_40 (and_40_out, and_8_out, d_ff_4_q, d_ff_14_q);
  D_Flip_Flop d_ff_15 (.D(in1), .clk(clock), .Q(d_ff_15_q));  // open: Qn, preset, reset
  D_Flip_Flop #(.trigger("high")) d_ff_16 (.D(or_1_out), .clk(clock), .Q(out3));  // open: Qn, preset, reset
  and and_41 (and_41_out, d_ff_17_q, and_1_out, not_13_out);
  D_Flip_Flop #(.trigger("high")) d_ff_17 (.D(and_33_out), .clk(and_9_out), .Q(d_ff_17_q));  // open: Qn, preset, reset
  and and_42 (and_42_out, d_ff_18_q, and_2_out, not_13_out);
  D_Flip_Flop #(.trigger("high")) d_ff_18 (.D(and_34_out), .clk(and_10_out), .Q(d_ff_18_q));  // open: Qn, preset, reset
  and and_43 (and_43_out, d_ff_19_q, and_3_out, not_13_out);
  D_Flip_Flop #(.trigger("high")) d_ff_19 (.D(and_35_out), .clk(and_11_out), .Q(d_ff_19_q));  // open: Qn, preset, reset
  and and_44 (and_44_out, d_ff_20_q, and_4_out, not_13_out);
  D_Flip_Flop #(.trigger("high")) d_ff_20 (.D(and_36_out), .clk(and_12_out), .Q(d_ff_20_q));  // open: Qn, preset, reset
  and and_45 (and_45_out, d_ff_21_q, and_5_out, not_13_out);
  D_Flip_Flop #(.trigger("high")) d_ff_21 (.D(and_37_out), .clk(and_13_out), .Q(d_ff_21_q));  // open: Qn, preset, reset
  and and_46 (and_46_out, d_ff_22_q, and_6_out, not_13_out);
  D_Flip_Flop #(.trigger("high")) d_ff_22 (.D(and_38_out), .clk(and_14_out), .Q(d_ff_22_q));  // open: Qn, preset, reset
  and and_47 (and_47_out, d_ff_23_q, and_7_out, not_13_out);
  D_Flip_Flop #(.trigger("high")) d_ff_23 (.D(and_39_out), .clk(and_15_out), .Q(d_ff_23_q));  // open: Qn, preset, reset
  and and_48 (and_48_out, d_ff_24_q, and_8_out, not_13_out);
  D_Flip_Flop #(.trigger("high")) d_ff_24 (.D(and_40_out), .clk(and_16_out), .Q(d_ff_24_q));  // open: Qn, preset, reset
  D_Flip_Flop d_ff_25 (.D(in0), .clk(clock), .Q(d_ff_25_q));  // open: Qn, preset, reset
  D_Flip_Flop #(.trigger("high")) d_ff_26 (.D(or_2_out), .clk(clock), .Q(out2));  // open: Qn, preset, reset
  or or_2 (or_2_out, and_41_out, and_42_out, and_43_out, and_44_out, and_45_out, and_46_out, and_47_out, and_48_out);
  D_Flip_Flop #(.trigger("high")) d_ff_27 (.D(or_3_out), .clk(clock), .Q(out1));  // open: Qn, preset, reset
  D_Flip_Flop #(.trigger("high")) d_ff_28 (.D(or_4_out), .clk(clock), .Q(out0));  // open: Qn, preset, reset
  and and_49 (and_49_out, and_1_out, d_ff_4_q, d_ff_15_q);
  D_Flip_Flop #(.trigger("high")) d_ff_29 (.D(and_49_out), .clk(and_9_out), .Q(d_ff_29_q));  // open: Qn, preset, reset
  and and_50 (and_50_out, and_2_out, d_ff_4_q, d_ff_15_q);
  D_Flip_Flop #(.trigger("high")) d_ff_30 (.D(and_50_out), .clk(and_10_out), .Q(d_ff_30_q));  // open: Qn, preset, reset
  and and_51 (and_51_out, and_3_out, d_ff_4_q, d_ff_15_q);
  D_Flip_Flop #(.trigger("high")) d_ff_31 (.D(and_51_out), .clk(and_11_out), .Q(d_ff_31_q));  // open: Qn, preset, reset
  and and_52 (and_52_out, and_4_out, d_ff_4_q, d_ff_15_q);
  D_Flip_Flop #(.trigger("high")) d_ff_32 (.D(and_52_out), .clk(and_12_out), .Q(d_ff_32_q));  // open: Qn, preset, reset
  and and_53 (and_53_out, and_5_out, d_ff_4_q, d_ff_15_q);
  D_Flip_Flop #(.trigger("high")) d_ff_33 (.D(and_53_out), .clk(and_13_out), .Q(d_ff_33_q));  // open: Qn, preset, reset
  and and_54 (and_54_out, and_6_out, d_ff_4_q, d_ff_15_q);
  D_Flip_Flop #(.trigger("high")) d_ff_34 (.D(and_54_out), .clk(and_14_out), .Q(d_ff_34_q));  // open: Qn, preset, reset
  and and_55 (and_55_out, and_7_out, d_ff_4_q, d_ff_15_q);
  D_Flip_Flop #(.trigger("high")) d_ff_35 (.D(and_55_out), .clk(and_15_out), .Q(d_ff_35_q));  // open: Qn, preset, reset
  and and_56 (and_56_out, and_8_out, d_ff_4_q, d_ff_15_q);
  D_Flip_Flop #(.trigger("high")) d_ff_36 (.D(and_56_out), .clk(and_16_out), .Q(d_ff_36_q));  // open: Qn, preset, reset
  or or_3 (or_3_out, and_57_out, and_58_out, and_59_out, and_60_out, and_61_out, and_62_out, and_63_out, and_64_out);
  and and_57 (and_57_out, d_ff_29_q, and_1_out, not_13_out);
  and and_58 (and_58_out, d_ff_30_q, and_2_out, not_13_out);
  and and_59 (and_59_out, d_ff_31_q, and_3_out, not_13_out);
  and and_60 (and_60_out, d_ff_32_q, and_4_out, not_13_out);
  and and_61 (and_61_out, d_ff_33_q, and_5_out, not_13_out);
  and and_62 (and_62_out, d_ff_34_q, and_6_out, not_13_out);
  and and_63 (and_63_out, d_ff_35_q, and_7_out, not_13_out);
  and and_64 (and_64_out, d_ff_36_q, and_8_out, not_13_out);
  and and_65 (and_65_out, and_1_out, d_ff_4_q, d_ff_25_q);
  D_Flip_Flop #(.trigger("high")) d_ff_37 (.D(and_65_out), .clk(and_9_out), .Q(d_ff_37_q));  // open: Qn, preset, reset
  and and_66 (and_66_out, and_2_out, d_ff_4_q, d_ff_25_q);
  D_Flip_Flop #(.trigger("high")) d_ff_38 (.D(and_66_out), .clk(and_10_out), .Q(d_ff_38_q));  // open: Qn, preset, reset
  and and_67 (and_67_out, and_3_out, d_ff_4_q, d_ff_25_q);
  D_Flip_Flop #(.trigger("high")) d_ff_39 (.D(and_67_out), .clk(and_11_out), .Q(d_ff_39_q));  // open: Qn, preset, reset
  and and_68 (and_68_out, and_4_out, d_ff_4_q, d_ff_25_q);
  D_Flip_Flop #(.trigger("high")) d_ff_40 (.D(and_68_out), .clk(and_12_out), .Q(d_ff_40_q));  // open: Qn, preset, reset
  and and_69 (and_69_out, and_5_out, d_ff_4_q, d_ff_25_q);
  D_Flip_Flop #(.trigger("high")) d_ff_41 (.D(and_69_out), .clk(and_13_out), .Q(d_ff_41_q));  // open: Qn, preset, reset
  and and_70 (and_70_out, and_6_out, d_ff_4_q, d_ff_25_q);
  D_Flip_Flop #(.trigger("high")) d_ff_42 (.D(and_70_out), .clk(and_14_out), .Q(d_ff_42_q));  // open: Qn, preset, reset
  and and_71 (and_71_out, and_7_out, d_ff_4_q, d_ff_25_q);
  D_Flip_Flop #(.trigger("high")) d_ff_43 (.D(and_71_out), .clk(and_15_out), .Q(d_ff_43_q));  // open: Qn, preset, reset
  and and_72 (and_72_out, and_8_out, d_ff_4_q, d_ff_25_q);
  D_Flip_Flop #(.trigger("high")) d_ff_44 (.D(and_72_out), .clk(and_16_out), .Q(d_ff_44_q));  // open: Qn, preset, reset
  or or_4 (or_4_out, and_73_out, and_74_out, and_75_out, and_76_out, and_77_out, and_78_out, and_79_out, and_80_out);
  and and_73 (and_73_out, d_ff_37_q, and_1_out, not_13_out);
  and and_74 (and_74_out, d_ff_38_q, and_2_out, not_13_out);
  and and_75 (and_75_out, d_ff_39_q, and_3_out, not_13_out);
  and and_76 (and_76_out, d_ff_40_q, and_4_out, not_13_out);
  and and_77 (and_77_out, d_ff_41_q, and_5_out, not_13_out);
  and and_78 (and_78_out, d_ff_42_q, and_6_out, not_13_out);
  and and_79 (and_79_out, d_ff_43_q, and_7_out, not_13_out);
  and and_80 (and_80_out, d_ff_44_q, and_8_out, not_13_out);

  // Notes on the sheet:
  //   3-bit address input pins
  //   Mode input pin
  //   4-bit data input pins
endmodule

module ADD (
  input  L3,
  input  L2,
  input  L1,
  input  L0,
  input  R3,
  input  R2,
  input  R1,
  input  R0,
  input  clock,
  input  command,
  output out3,
  output out2,
  output out1,
  output out0,
  output status0,
  output status1,
  output status2
);

  wire and_1_out, and_2_out, and_3_out, and_4_out, and_5_out, and_6_out, and_7_out, and_8_out, and_9_out,
       and_10_out, and_11_out, and_12_out, and_13_out, and_14_out, and_15_out, and_16_out, and_17_out,
       and_18_out, and_19_out, and_20_out, and_21_out, and_22_out, and_23_out, and_24_out, and_25_out,
       and_26_out, and_27_out, and_31_out, and_32_out, and_33_out, and_34_out, and_35_out, and_36_out,
       and_37_out, and_38_out, not_1_out, not_2_out, not_3_out, not_4_out, not_5_out, not_6_out, not_7_out,
       not_8_out, not_9_out, not_10_out, not_11_out, or_1_out, or_2_out, or_3_out, or_4_out, or_5_out,
       or_7_out, or_8_out, or_9_out, or_10_out, or_11_out, or_12_out, or_13_out, xor_1_out, xor_3_out,
       xor_5_out, xor_8_out, xor_9_out, xor_10_out, xor_11_out, xor_12_out, xor_13_out, xor_14_out;

  and and_1 (and_1_out, and_3_out, and_16_out);
  and and_2 (and_2_out, xor_1_out, or_2_out);
  or or_1 (or_1_out, and_1_out, and_2_out);
  xor xor_1 (xor_1_out, and_3_out, and_16_out);
  xor xor_2 (out3, xor_1_out, or_2_out);
  and and_3 (and_3_out, L3, clock);
  and and_4 (and_4_out, and_5_out, and_19_out);
  and and_5 (and_5_out, L2, clock);
  and and_6 (and_6_out, xor_3_out, or_3_out);
  or or_2 (or_2_out, and_4_out, and_6_out);
  and and_7 (and_7_out, L1, clock);
  xor xor_3 (xor_3_out, and_5_out, and_19_out);
  xor xor_4 (out2, xor_3_out, or_3_out);
  and and_8 (and_8_out, L0, clock);
  and and_9 (and_9_out, and_7_out, and_22_out);
  or or_3 (or_3_out, and_9_out, and_10_out);
  xor xor_5 (xor_5_out, and_7_out, and_22_out);
  and and_10 (and_10_out, xor_5_out, and_12_out);
  xor xor_6 (out1, xor_5_out, and_12_out);
  not not_1 (not_1_out, or_1_out);
  and and_11 (and_11_out, and_3_out, and_16_out);
  not not_2 (not_2_out, or_4_out);
  or or_4 (or_4_out, and_3_out, and_16_out);
  and and_12 (and_12_out, and_8_out, and_26_out);
  and and_13 (and_13_out, and_11_out, not_1_out);
  and and_14 (and_14_out, not_2_out, or_1_out);
  and and_15 (and_15_out, R3, not_11_out);
  and and_16 (and_16_out, clock, or_9_out);
  xor xor_7 (out0, and_8_out, and_26_out);
  not not_3 (not_3_out, out0);
  not not_4 (not_4_out, out1);
  not not_5 (not_5_out, out3);
  not not_6 (not_6_out, out2);
  or or_5 (or_5_out, and_13_out, and_14_out);
  and and_17 (and_17_out, not_7_out, 1'b0);
  and and_18 (and_18_out, R2, not_11_out);
  and and_19 (and_19_out, clock, or_10_out);
  and and_20 (and_20_out, xor_8_out, or_8_out);
  // OR_Gate or_6 has open pins: in0=and_17_out, in1=and_20_out, out=open
  and and_21 (and_21_out, R1, not_11_out);
  and and_22 (and_22_out, clock, or_11_out);
  and and_23 (and_23_out, out3, out3);
  and and_24 (and_24_out, not_3_out, not_4_out, not_5_out, not_6_out);
  or or_7 (or_7_out, or_1_out, or_5_out);
  xor xor_8 (xor_8_out, not_7_out, 1'b0);
  xor xor_9 (xor_9_out, xor_8_out, or_8_out);
  and and_25 (and_25_out, R0, not_11_out);
  and and_26 (and_26_out, clock, or_13_out);
  and and_27 (and_27_out, not_8_out, 1'b0);
  and and_28 (status0, clock, and_23_out);
  and and_29 (status1, clock, and_24_out);
  and and_30 (status2, clock, or_7_out);
  not not_7 (not_7_out, R3);
  and and_31 (and_31_out, xor_10_out, or_12_out);
  or or_8 (or_8_out, and_27_out, and_31_out);
  or or_9 (or_9_out, and_15_out, and_32_out);
  not not_8 (not_8_out, R2);
  not not_9 (not_9_out, R1);
  not not_10 (not_10_out, R0);
  xor xor_10 (xor_10_out, not_8_out, 1'b0);
  xor xor_11 (xor_11_out, xor_10_out, or_12_out);
  or or_10 (or_10_out, and_18_out, and_34_out);
  and and_32 (and_32_out, xor_9_out, command);
  or or_11 (or_11_out, and_21_out, and_36_out);
  and and_33 (and_33_out, not_9_out, 1'b0);
  or or_12 (or_12_out, and_33_out, and_35_out);
  and and_34 (and_34_out, xor_11_out, command);
  or or_13 (or_13_out, and_25_out, and_37_out);
  xor xor_12 (xor_12_out, not_9_out, 1'b0);
  and and_35 (and_35_out, xor_12_out, and_38_out);
  and and_36 (and_36_out, xor_13_out, command);
  and and_37 (and_37_out, xor_14_out, command);
  xor xor_13 (xor_13_out, xor_12_out, and_38_out);
  and and_38 (and_38_out, not_10_out, 1'b1);
  xor xor_14 (xor_14_out, not_10_out, 1'b1);
  not not_11 (not_11_out, command);

  // Notes on the sheet:
  //   Venicia LeBlanc
  //   ID: 261054489
  //   Status output
  //   bit 0 = negative
  //   bit 1 = zero
  //   bit 2 = overflow
  //   0 constant
  //   1 constant
  //   Add/Sub command
endmodule

module MAR (
);


  // Notes on the sheet:
  //   store address register
  //   of next instruction to be exec
endmodule

module MBR (
  input  adr,
  output b3,
  output b2,
  output b1,
  output b0
);

  RAMx ramx_1 (
    .adr0(adr), .out3(b3), .out2(b2), .out1(b1), .out0(b0));  // open: adr2, adr1, mode, clock, in3, in2, in1, in0

  // Notes on the sheet:
  //   memory buffer reg
  //   data fecthed from memory
  //   bits fetched from adr?
endmodule

module IR (
  input  in_1,
  input  in_2,
  input  in_3,
  input  in_4
);

  wire A0, A1, add, load, not_1_out, not_2_out, not_3_out, not_4_out, R0, R1, save, sub;

  not not_1 (not_1_out, in_1);
  and and_1 (load, not_1_out, not_2_out);
  not not_2 (not_2_out, in_2);
  not not_3 (not_3_out, in_1);
  and and_2 (save, not_3_out, in_2);
  and and_3 (add, in_1, not_4_out);
  not not_4 (not_4_out, in_2);
  and and_4 (sub, in_1, in_2);
  and and_5 (R0, ~in_3, ~in_3);  // AND_Gate
  buf and_6 (R1, in_3);  // AND_Gate
  and and_7 (A0, ~in_4, ~in_4);  // AND_Gate
  buf and_8 (A1, in_4);  // AND_Gate
endmodule

module PC (
  input  in_en,
  input  adr3,
  input  adr2,
  input  adr1,
  input  adr0,
  input  en,
  input  clock,
  input  rw,
  output out3,
  output out2,
  output out1,
  output out0
);

  wire add_1_out0, add_1_out1, add_1_out2, add_1_out3, and_1_out, and_2_out, and_3_out, and_4_out, and_5_out,
       and_6_out, and_7_out, and_8_out, not_1_out, or_1_out, or_2_out, or_3_out, or_4_out;

  not not_1 (not_1_out, in_en);
  and and_1 (and_1_out, not_1_out, add_1_out3);
  and and_2 (and_2_out, in_en, adr3);
  and and_3 (and_3_out, in_en, adr2);
  and and_4 (and_4_out, in_en, adr1);
  and and_5 (and_5_out, in_en, adr0);
  and and_6 (and_6_out, not_1_out, add_1_out2);
  and and_7 (and_7_out, not_1_out, add_1_out1);
  and and_8 (and_8_out, not_1_out, add_1_out0);
  or or_1 (or_1_out, and_1_out, and_2_out);
  or or_2 (or_2_out, and_6_out, and_3_out);
  or or_3 (or_3_out, and_7_out, and_4_out);
  or or_4 (or_4_out, and_8_out, and_5_out);
  reg4bits reg4bits_1 (
    .d3(or_1_out), .d2(or_2_out), .d1(or_3_out), .d0(or_4_out), .en(en), .clk(clock), .rw(rw), .b3(out3),
    .b2(out2), .b1(out1), .b0(out0));
  ADD add_1 (
    .out0(add_1_out0), .out3(add_1_out3), .out2(add_1_out2), .out1(add_1_out1), .R0(1'b1), .clock(clock),
    .L3(out3), .L2(out2), .L1(out1), .L0(out0));  // open: status0, status1, status2, R3, R2, R1, command

  // Notes on the sheet:
  //   address of next instruction to be exec
endmodule

module CU (
  input  clock,
  input  ir3,
  input  ir2,
  input  ir1,
  input  ir0,
  input  s3,
  input  s2,
  input  s1,
  input  s0,
  output reg0write,
  output reg0en,
  output reg1write,
  output reg1en,
  output adr0write,
  output adr0en,
  output adr1write,
  output adr1en,
  output add_sub
);

  wire add, adr0, and_6_out, and_7_out, and_8_out, and_9_out, and_10_out, and_11_out, and_12_out, and_13_out,
       and_14_out, and_15_out, and_16_out, and_17_out, and_18_out, and_19_out, and_20_out, and_21_out,
       and_22_out, and_23_out, and_24_out, and_25_out, and_26_out, and_27_out, and_28_out, and_29_out,
       and_30_out, and_31_out, and_32_out, and_33_out, and_34_out, and_35_out, and_36_out, and_37_out, halt,
       load, not_3_out, not_4_out, not_5_out, not_6_out, not_7_out, not_8_out, not_9_out, R0, save, sub;

  and and_1 (halt, ir0, ir1, ir2, ir3);
  not not_1 (adr0, ir0);
  not not_2 (R0, ir1);
  not not_3 (not_3_out, ir2);
  and and_2 (load, not_3_out, clock, not_4_out);
  not not_4 (not_4_out, ir3);
  and and_3 (save, ir2, clock, not_5_out);
  not not_5 (not_5_out, ir3);
  not not_6 (not_6_out, ir2);
  and and_4 (add, not_6_out, clock, ir3);
  and and_5 (sub, ir2, ir3, not_7_out);
  not not_7 (not_7_out, halt);
  buf and_6 (and_6_out, clock);  // AND_Gate
  buf and_7 (and_7_out, clock);  // AND_Gate
  buf and_8 (and_8_out, clock);  // AND_Gate
  buf and_9 (and_9_out, clock);  // AND_Gate
  and and_10 (and_10_out, add, R0);
  and and_11 (and_11_out, and_10_out, and_9_out);
  and and_12 (and_12_out, and_10_out, and_8_out);
  and and_13 (and_13_out, and_10_out, and_7_out);
  and and_14 (and_14_out, add, ir1);
  and and_15 (and_15_out, and_14_out, and_9_out);
  and and_16 (and_16_out, and_14_out, and_8_out);
  and and_17 (and_17_out, and_14_out, and_7_out);
  and and_18 (and_18_out, and_14_out, and_6_out);
  and and_19 (and_19_out, sub, R0);
  and and_20 (and_20_out, and_19_out, and_9_out);
  and and_21 (and_21_out, and_19_out, and_8_out);
  and and_22 (and_22_out, and_19_out, and_7_out);
  and and_23 (and_23_out, sub, ir1);
  and and_24 (and_24_out, and_23_out, and_9_out);
  and and_25 (and_25_out, and_23_out, and_8_out);
  and and_26 (and_26_out, and_23_out, and_7_out);
  and and_27 (and_27_out, and_23_out, and_6_out);
  and and_28 (and_28_out, load, R0, adr0);
  and and_29 (and_29_out, load, R0, ir0);
  and and_30 (and_30_out, load, ir1, adr0);
  and and_31 (and_31_out, load, ir1, ir0);
  and and_32 (and_32_out, save, R0, adr0);
  and and_33 (and_33_out, save, R0, ir0);
  and and_34 (and_34_out, save, ir1, adr0);
  and and_35 (and_35_out, save, ir1, ir0);
  not not_8 (not_8_out, and_12_out);
  not not_9 (not_9_out, and_17_out);
  or or_1 (reg0write, and_28_out, and_29_out, and_13_out, and_18_out, and_22_out, and_27_out);
  and and_36 (and_36_out, and_10_out, not_8_out);
  and and_37 (and_37_out, and_14_out, not_9_out);
  or or_2 (reg0en, and_32_out, and_33_out, and_11_out, and_15_out, and_20_out, and_24_out);
  or or_3 (reg1write, and_30_out, and_31_out);
  or or_4 (reg1en, and_34_out, and_35_out, and_16_out, and_25_out);
  or or_5 (adr0write, and_32_out, and_34_out);
  or or_6 (adr0en, and_28_out, and_30_out);
  or or_7 (adr1write, and_33_out, and_35_out);
  or or_8 (adr1en, and_29_out, and_31_out);
  or or_9 (add_sub, and_36_out, and_37_out, and_21_out, and_26_out);

  // Other names for the same wires on the sheet: adr1 = ir0; R1 = ir1
endmodule
